# Fritzing sketch CNMB3-A (saved by Fritzing 0.9.8b)
circuit board: 5cm x 8.65cm
breadboards: 1

parts:
  Part1 = Arduino Nano (Rev3.0) (ICSP)
  WeMos_D1_Mini1 = WeMos D1 Mini
  J5 = screw terminal, 9 pins
  J14 = double row female pin header, 8 pins [form="♀ (female)"]
  J4 = screw terminal, 9 pins

nets:
  N1: Part1.D1/TX, Part1.A5, WeMos_D1_Mini1.D1, J5.pin8, J4.pin4
  N2: Part1.D0/RX, WeMos_D1_Mini1.D0, J14.pin6
  N3: Part1.GND, WeMos_D1_Mini1.G, J14.pin5, J4.pin3, J4.pin9
  N4: Part1.D2, Part1.A4, WeMos_D1_Mini1.D2, J5.pin7, J4.pin5
  N5: Part1.D3, WeMos_D1_Mini1.D3, J5.pin6
  N6: Part1.D4, WeMos_D1_Mini1.D4, J5.pin5
  N7: Part1.D5, WeMos_D1_Mini1.D5, J5.pin4
  N8: Part1.D6, WeMos_D1_Mini1.D6, J5.pin3
  N9: Part1.D7, WeMos_D1_Mini1.D7, J5.pin2
  N10: Part1.D8, WeMos_D1_Mini1.D8, J5.pin1, J14.pin7
  VIN: Part1.VIN, WeMos_D1_Mini1.5V, J5.pin9, J14.pin4, J4.pin2
  3V3: Part1.3V3, WeMos_D1_Mini1.3V3, J14.pin3
  N11: J14.pin1, J4.pin7
  N12: J14.pin2, J4.pin6
  N13: J14.pin8, J4.pin8

notes:
  12v
  5v
  0V
  SDA
  SCL
  D8
  D7
  D6
  D5
  D4
  D3
  D2
  D1
  C
  NO
  NC
  5
  3
  0
  S
  D
  A
  B
  (A0)
  ------
  ----
  wemos SDA
  wemos SCL
  (D8)
  Relay
