# Fritzing sketch CNMB3-B (saved by Fritzing 0.9.8b)
circuit board: 4.9cm x 5.7cm
breadboards: 1

parts:
  LED1 = LED - 5mm [color="Red (633nm)" current=0.030 package="5 mm [THT]"]
  IC1 = IC, DIP package, 16 pins [chip_label=IC]
  J10 = double row female pin header, 8 pins [form="♀ (female)"]
  Q1 = NPN-Transistor [package="TO92 [THT]"]
  R2 = Resistor [tolerance=±5% power=0.25 resistance=220 package=THT]
  LED3 = RGB LED - (4 legs) [package="5 mm [THT]"]
  LED4 = RGB LED - (4 legs) [package="5 mm [THT]"]
  LED5 = RGB LED - (4 legs) [package="5 mm [THT]"]
  D1 = Rectifier Diode [part_number=1N4001 package="300 mil [THT]"]
  R3 = Resistor [tolerance=±5% power=0.25 resistance=220 package=THT]

nets:
  N1: LED1.cathode, R3.Pin_0
  N2: LED1.anode, J10.pin2
  N3: IC1.pin1, J10.pin3
  N4: IC1.pin3, J10.pin5
  N5: IC1.pin5, J10.pin4
  N6: IC1.pin8, J10.pin1, LED3.common_anode, LED4.common_anode, LED5.common_anode, D1.cathode
  N7: IC1.pin9, Q1.C, D1.anode
  N8: J10.pin6, R2.Pin_1
  N9: J10.pin7, LED3.blue_cathode
  N10: J10.pin8, Q1.E, LED3.green_cathode, LED4.green_cathode, LED5.green_cathode, R3.Pin_1
  N11: Q1.B, R2.Pin_0
  N12: LED3.red_cathode, LED4.blue_cathode
  N13: LED4.red_cathode, LED5.blue_cathode

notes:
  POWER
  DOMOTA
  by cone
  C A 3 5
  B D S 0
  --
  c
  STATUS
